// Logisim project Pong.circ as structural Verilog: 5 circuits, main circuit main
module main (
);

  wire ball_1_resetout, button_1_out, button_2_out, button_3_out, button_4_out, clock_1_out,
       colisions_1_resut, Reset_out;
  wire [3:0] ball_1_x;
  wire [7:0] ball_1_y, demultiplexer_1_out0, demultiplexer_1_out1, demultiplexer_1_out2,
       demultiplexer_1_out3, demultiplexer_1_out4, demultiplexer_1_out5, demultiplexer_1_out6,
       demultiplexer_1_out7, demultiplexer_1_out8, demultiplexer_1_out9, demultiplexer_1_out10,
       demultiplexer_1_out11, demultiplexer_1_out12, demultiplexer_1_out13, demultiplexer_1_out14,
       demultiplexer_1_out15, or_1_out, or_2_out, paddle_1_result, paddle_2_result;

  Button Reset (.out(Reset_out));
  Clock clock_1 (.out(clock_1_out));
  // LedBar #(.inputtype("row"), .matrixcols(21)) ledbar_1: pin names not known
  scoreboard scoreboard_1 (.resetButton(Reset_out), .resetBall(ball_1_resetout), .xBallPos(ball_1_x));  // open: Result
  paddle paddle_1 (.down(button_2_out), .up(button_1_out), .reset(ball_1_resetout), .Result(paddle_1_result));
  Button button_1 (.out(button_1_out));
  Button button_2 (.out(button_2_out));
  Ball ball_1 (
    .resetIn(Reset_out), .Clock(clock_1_out), .xDirectReverse(colisions_1_resut), .resetOut(ball_1_resetout),
    .x(ball_1_x), .y(ball_1_y));
  assign or_1_out = paddle_1_result | demultiplexer_1_out0;  // OR_Gate or_1, 8 bits wide
  DotMatrix #(.matrixcols(16), .matrixrows(8)) dotmatrix_1 (
    .col0(or_1_out), .col1(demultiplexer_1_out1), .col2(demultiplexer_1_out2), .col3(demultiplexer_1_out3),
    .col4(demultiplexer_1_out4), .col5(demultiplexer_1_out5), .col6(demultiplexer_1_out6),
    .col7(demultiplexer_1_out7), .col8(demultiplexer_1_out8), .col9(demultiplexer_1_out9),
    .col10(demultiplexer_1_out10), .col11(demultiplexer_1_out11), .col12(demultiplexer_1_out12),
    .col13(demultiplexer_1_out13), .col14(demultiplexer_1_out14), .col15(or_2_out));
  Demultiplexer #(.select(4), .width(8)) demultiplexer_1 (
    .out0(demultiplexer_1_out0), .out1(demultiplexer_1_out1), .out2(demultiplexer_1_out2),
    .out3(demultiplexer_1_out3), .out4(demultiplexer_1_out4), .out5(demultiplexer_1_out5),
    .out6(demultiplexer_1_out6), .out7(demultiplexer_1_out7), .out8(demultiplexer_1_out8),
    .out9(demultiplexer_1_out9), .out10(demultiplexer_1_out10), .out11(demultiplexer_1_out11),
    .out12(demultiplexer_1_out12), .out13(demultiplexer_1_out13), .out14(demultiplexer_1_out14),
    .out15(demultiplexer_1_out15), .in(ball_1_y), .sel(ball_1_x));
  assign or_2_out = demultiplexer_1_out15 | paddle_2_result;  // OR_Gate or_2, 8 bits wide
  paddle paddle_2 (.down(button_4_out), .up(button_3_out), .reset(ball_1_resetout), .Result(paddle_2_result));
  Button button_3 (.out(button_3_out));
  Button button_4 (.out(button_4_out));
  Colisions colisions_1 (
    .leftPaddle(paddle_2_result), .rightPaddle(paddle_1_result), .x(ball_1_x), .y(ball_1_y),
    .Resut(colisions_1_resut));
endmodule

module paddle (
  input  reset,
  input  up,
  input  down,
  output [7:0] Result
);

  wire comparator_1_eq, comparator_2_eq, not_1_out, not_2_out, or_1_out;
  wire [7:0] controlled_buffer_1_out, controlled_buffer_3_out, controlled_buffer_4_out, shifter_1_out,
       shifter_2_out;

  Shifter shifter_1 (.in(Result), .\dist (3'b001), .out(shifter_1_out));
  Comparator comparator_1 (.a(Result), .b(8'he0), .eq(comparator_1_eq));  // open: gt, lt
  Shifter #(.shift("lr")) shifter_2 (.in(Result), .\dist (3'b001), .out(shifter_2_out));
  Comparator comparator_2 (.a(Result), .b(8'h7), .eq(comparator_2_eq));  // open: gt, lt
  assign controlled_buffer_1_out = not_1_out ? shifter_1_out : 8'bz;  // Controlled_Buffer controlled_buffer_1
  not not_1 (not_1_out, comparator_1_eq);
  assign controlled_buffer_1_out = comparator_1_eq ? 8'he0 : 8'bz;  // Controlled_Buffer controlled_buffer_2
  assign controlled_buffer_3_out = not_2_out ? shifter_2_out : 8'bz;  // Controlled_Buffer controlled_buffer_3
  assign controlled_buffer_4_out = down ? controlled_buffer_3_out : 8'bz;  // Controlled_Buffer controlled_buffer_4
  not not_2 (not_2_out, comparator_2_eq);
  assign controlled_buffer_3_out = comparator_2_eq ? 8'h7 : 8'bz;  // Controlled_Buffer controlled_buffer_5
  assign controlled_buffer_4_out = up ? controlled_buffer_1_out : 8'bz;  // Controlled_Buffer controlled_buffer_6
  assign controlled_buffer_4_out = reset ? 8'h1c : 8'bz;  // Controlled_Buffer controlled_buffer_7
  or or_1 (or_1_out, reset, up, down);
  Register register_1 (.D(controlled_buffer_4_out), .en(or_1_out), .clk(or_1_out), .Q(Result));  // open: clr
endmodule

module Ball (
  input  resetIn,
  input  Clock,
  input  xDirectReverse,
  output resetOut,
  output [3:0] x,
  output [7:0] y
);

  wire comparator_1_eq, comparator_2_eq, counter_1_carry, counter_2_carry, d_ff_1_q, d_ff_2_q, not_1_out,
       not_2_out, or_2_out, xor_1_out;
  wire [2:0] counter_2_q;

  xor xor_1 (xor_1_out, xDirectReverse, not_1_out);
  Counter #(.max('hf), .ongoal("stay"), .width(4)) counter_1 (
    .load(resetOut), .up(xor_1_out), .clk(Clock), .D(4'b1000), .carry(counter_1_carry), .Q(x));  // open: clr, count
  Counter #(.max('h7), .ongoal("stay"), .width(3)) counter_2 (
    .load(resetOut), .up(not_2_out), .clk(Clock), .D(3'b100), .carry(counter_2_carry), .Q(counter_2_q));  // open: clr, count
  or or_1 (resetOut, resetIn, or_2_out);
  not not_1 (not_1_out, d_ff_1_q);
  D_Flip_Flop d_ff_1 (.D(not_1_out), .clk(counter_1_carry), .Q(d_ff_1_q));  // open: Qn, preset, reset
  not not_2 (not_2_out, d_ff_2_q);
  D_Flip_Flop d_ff_2 (.D(not_2_out), .clk(counter_2_carry), .Q(d_ff_2_q));  // open: Qn, preset, reset
  Shifter shifter_1 (.in(8'h1), .\dist (counter_2_q), .out(y));
  or or_2 (or_2_out, comparator_1_eq, comparator_2_eq);
  Comparator #(.width(4)) comparator_1 (.a(4'b0000), .b(x), .eq(comparator_1_eq));  // open: gt, lt
  Comparator #(.width(4)) comparator_2 (.a(4'b1111), .b(x), .eq(comparator_2_eq));  // open: gt, lt
endmodule

module Colisions (
  input  [7:0] leftPaddle,
  input  [7:0] rightPaddle,
  input  [3:0] x,
  input  [7:0] y,
  output Resut
);

  wire and_1_out, and_2_out, comparator_1_eq, comparator_2_eq, comparator_3_eq, comparator_4_eq, not_1_out,
       or_3_out;
  wire [7:0] or_1_out, or_2_out;

  assign or_1_out = leftPaddle | y;  // OR_Gate or_1, 8 bits wide
  assign or_2_out = rightPaddle | y;  // OR_Gate or_2, 8 bits wide
  Comparator comparator_1 (.a(leftPaddle), .b(or_1_out), .eq(comparator_1_eq));  // open: gt, lt
  and and_1 (and_1_out, comparator_1_eq, comparator_2_eq);
  Comparator #(.width(4)) comparator_2 (.a(x), .b(4'b1110), .eq(comparator_2_eq));  // open: gt, lt
  Comparator comparator_3 (.a(rightPaddle), .b(or_2_out), .eq(comparator_3_eq));  // open: gt, lt
  and and_2 (and_2_out, comparator_3_eq, comparator_4_eq);
  Comparator #(.width(4)) comparator_4 (.a(x), .b(4'b0001), .eq(comparator_4_eq));  // open: gt, lt
  not not_1 (not_1_out, Resut);
  D_Flip_Flop d_ff_1 (.D(not_1_out), .clk(or_3_out), .Q(Resut));  // open: Qn, preset, reset
  or or_3 (or_3_out, and_1_out, and_2_out);
endmodule

module scoreboard (
  input  resetButton,
  input  resetBall,
  input  [3:0] xBallPos,
  output [20:0] Result
);

  wire and_1_out, comparator_1_eq, comparator_2_eq, comparator_3_eq, or_1_out, or_2_out;
  wire [4:0] counter_1_q;

  and and_1 (and_1_out, resetButton, resetBall);
  Comparator #(.width(4)) comparator_1 (.a(4'b1111), .b(xBallPos), .eq(comparator_1_eq));  // open: gt, lt
  Comparator #(.width(4)) comparator_2 (.a(4'b1111), .b(xBallPos), .eq(comparator_2_eq));  // open: gt, lt
  Comparator #(.width(4)) comparator_3 (.a(4'b0000), .b(xBallPos), .eq(comparator_3_eq));  // open: gt, lt
  Counter #(.max('h1f), .ongoal("stay"), .width(5)) counter_1 (
    .load(and_1_out), .up(comparator_1_eq), .clk(or_1_out), .D(5'b01010), .Q(counter_1_q));  // open: clr, count, carry
  or or_1 (or_1_out, and_1_out, or_2_out);
  or or_2 (or_2_out, comparator_2_eq, comparator_3_eq);
  Shifter #(.width(21)) shifter_1 (.in(21'h1), .\dist (counter_1_q), .out(Result));
endmodule
